// Logisim project DSD_CEP.circ as structural Verilog: 6 circuits, main circuit Half_adder
module main (
  input  Cin,
  input  [7:0] in_2,
  input  [7:0] in_3,
  output Cout,
  output [7:0] out_5,
  output [7:0] out_6,
  output [7:0] out_7
);

  wire [7:0] carry_generator_1_c0;

  P_G p_g_1 (.in_1(in_2), .in_2(in_3), .out_3(out_6), .out_4(out_7));
  Carry_Generator carry_generator_1 (
    .G(out_7), .in_2(out_6), .Cin(Cin), .C8__Cout(Cout), .C7(carry_generator_1_c0[7]),
    .C6(carry_generator_1_c0[6]), .C5(carry_generator_1_c0[5]), .C4(carry_generator_1_c0[4]),
    .C3(carry_generator_1_c0[3]), .C2(carry_generator_1_c0[2]), .C1(carry_generator_1_c0[1]),
    .C0(carry_generator_1_c0[0]));
  Adder adder_1 (.in_1(out_6), .C(carry_generator_1_c0), .out_3(out_5));

  // Notes on the sheet:
  //   A
  //   B
  //   P
  //   G
  //   SUM
endmodule

module Half_adder (
  input  A,
  input  B,
  output S,
  output C
);

  xor xor_1 (S, A, B);
  and and_1 (C, B, A);
endmodule

module Full_Adder (
  input  A,
  input  B,
  input  Cin,
  output SUM,
  output CARRY
);

  wire half_adder_1_c, half_adder_1_s, half_adder_2_c;

  Half_adder half_adder_1 (.A(A), .B(B), .S(half_adder_1_s), .C(half_adder_1_c));
  Half_adder half_adder_2 (.A(half_adder_1_s), .B(Cin), .S(SUM), .C(half_adder_2_c));
  or or_1 (CARRY, half_adder_2_c, half_adder_1_c);
endmodule

module Carry_Generator (
  input  [7:0] G,
  input  [7:0] in_2,
  input  Cin,
  output C8__Cout,
  output C7,
  output C6,
  output C5,
  output C4,
  output C3,
  output C2,
  output C1,
  output C0
);

  wire and_1_out, and_2_out, and_3_out, and_4_out, and_5_out, and_6_out, and_7_out, and_8_out;

  or or_1 (C1, G[0], and_1_out);
  and and_1 (and_1_out, in_2[0], Cin);
  or or_2 (C2, G[1], and_2_out);
  and and_2 (and_2_out, in_2[1], C1);
  and and_3 (and_3_out, in_2[2], C2);
  or or_3 (C3, G[2], and_3_out);
  and and_4 (and_4_out, in_2[3], C3);
  or or_4 (C4, G[3], and_4_out);
  and and_5 (and_5_out, in_2[4], C4);
  and and_6 (and_6_out, in_2[5], C5);
  or or_5 (C5, G[4], and_5_out);
  or or_6 (C6, G[5], and_6_out);
  and and_7 (and_7_out, in_2[6], C6);
  or or_7 (C7, G[6], and_7_out);
  and and_8 (and_8_out, in_2[7], C7);
  or or_8 (C8__Cout, G[7], and_8_out);

  assign C0 = Cin;

  // Notes on the sheet:
  //   P
endmodule

module Adder (
  input  [7:0] in_1,
  input  [7:0] C,
  output [7:0] out_3
);

  xor xor_1 (out_3[0], in_1[0], C[0]);
  xor xor_2 (out_3[1], in_1[1], C[1]);
  xor xor_3 (out_3[2], in_1[2], C[2]);
  xor xor_4 (out_3[3], in_1[3], C[3]);
  xor xor_5 (out_3[4], in_1[4], C[4]);
  xor xor_6 (out_3[5], in_1[5], C[5]);
  xor xor_7 (out_3[6], in_1[6], C[6]);
  xor xor_8 (out_3[7], in_1[7], C[7]);

  // Notes on the sheet:
  //   P
  //   SUM
endmodule

module P_G (
  input  [7:0] in_1,
  input  [7:0] in_2,
  output [7:0] out_3,
  output [7:0] out_4
);

  Half_adder half_adder_1 (.A(in_1[0]), .B(in_2[0]), .S(out_3[0]), .C(out_4[0]));
  Half_adder half_adder_2 (.A(in_1[1]), .B(in_2[1]), .S(out_3[1]), .C(out_4[1]));
  Half_adder half_adder_3 (.A(in_1[2]), .B(in_2[2]), .S(out_3[2]), .C(out_4[2]));
  Half_adder half_adder_4 (.A(in_1[3]), .B(in_2[3]), .S(out_3[3]), .C(out_4[3]));
  Half_adder half_adder_5 (.A(in_1[4]), .B(in_2[4]), .S(out_3[4]), .C(out_4[4]));
  Half_adder half_adder_6 (.A(in_1[5]), .B(in_2[5]), .S(out_3[5]), .C(out_4[5]));
  Half_adder half_adder_7 (.A(in_1[6]), .B(in_2[6]), .S(out_3[6]), .C(out_4[6]));
  Half_adder half_adder_8 (.A(in_1[7]), .B(in_2[7]), .S(out_3[7]), .C(out_4[7]));

  // Notes on the sheet:
  //   A
  //   B
  //   P
  //   G
endmodule
